# Fritzing sketch Block Diagram (saved by Fritzing 0.9.3b)
breadboards: 1

parts:
  Capacitive_Soil_Moisture_Sensor1 = DFRobot Capacitive Soil Moisture Sensor V1.0 [part_number=SEN0193]
  WATER_PUMP = water pump/motor
  KY-1 = Keyes Relay [package=THT]
  F1 = Fan - Ventilador [package=THT]  # not connected
  LCD_I2C = LCD1602-I2C
  5V_DC = Power Jack [package=power_jack_combo]
  220V = Power Jack [package=power_jack_combo]
  KY-2 = Keyes Relay [package=THT]
  KY-3 = Keyes Relay [package=THT]
  KY-4 = Keyes Relay [package=THT]
  DHT11_1 = DHT11 module
  Humidifier_Plate = WG3166A Atomizer
  F2 = Fan - Ventilador [package=THT]
  BULB1 = LEDs [package=led10mm]
  U1 = ESP32S-HiLetgo [part_number=ESP32S-HiLetgo]
  LDR = KY-018 Photoresistor Module [package="Breakout board"]
  Water_Level_Sensor1 = Water Level Sensor

nets:
  N1: Capacitive_Soil_Moisture_Sensor1.A, U1.GPIO33
  VCC: Capacitive_Soil_Moisture_Sensor1.VCC, KY-1.power, LCD_I2C.VCC, KY-2.power, KY-3.power, KY-4.power, DHT11_1.VCC, U1.VIN, LDR.Vin, Water_Level_Sensor1.VCC
  GND: Capacitive_Soil_Moisture_Sensor1.GND, KY-1.ground, LCD_I2C.GND, KY-2.ground, KY-3.ground, KY-4.ground, DHT11_1.GND, U1.GND, LDR.-, Water_Level_Sensor1.GND
  GND_2: WATER_PUMP.pin_1, 5V_DC.GND, Humidifier_Plate.E1, F2.GND
  N2: WATER_PUMP.pin_2, KY-1.NO
  N3: KY-1.signal, U1.GPIO14
  N4: KY-1.C, 5V_DC.PWR, KY-2.C, KY-3.C, KY-4.C
  N5: 5V_DC.GNDBREAK, U1.GPIO10
  N6: 220V.GNDBREAK, BULB1.A
  N7: 220V.PWR, BULB1.C
  N8: KY-2.signal, U1.GPIO26
  N9: KY-3.signal, U1.GPIO27
  N10: KY-3.NO, Humidifier_Plate.E2
  N11: KY-4.signal, U1.GPIO12
  N12: KY-4.NO, F2.5V
  N13: DHT11_1.DATA, U1.GPIO25
  N14: U1.GPIO35, Water_Level_Sensor1.SIG
  N15: U1.GPIO32, LDR.S

custom parts:
  DFRobot Capacitive Soil Moisture Sensor V1.0: DFRobot Capacitive Soil Moisture Sensor V1.0 This product measures soil moisture levels by capacitive sensing, rather than resistive sensing like other types of moisture sensor. It is made of a corrosion resistant material giving it a long service life. Insert it into soil and impress your friends with the real-time soil moisture data! The product includes an on-board voltage regulator which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
  water pump/motor: WATER PUMP BY ARDUBLOCKTR
  Keyes Relay: The Keyes 5V relay module is suitable for SCM development, home appliance control. It uses a 5V~12V TIL control signal which can control DC / AC signal.
  Fan - Ventilador: Ventilador de 2 pines, se encuentra comunmente en computadoras de escritorio
  LCD1602-I2C: A standard character display, usually with 2x16 characters. Comes in many colors with LCM1602 IIC attached.
  DHT11 module: https://cdn-learn.adafruit.com/downloads/pdf/dht.pdf DHT11 black pcb module reference by:https://github.com/adafruit/Fritzing-Library/blob/master/parts/DHT11%20Humitidy%20and%20Temperature%20Sensor.fzpz
  WG3166A Atomizer: 20mm 113KHz Ultrasonic Mist Maker Fogger Atomizer Ceramic Discs with Power Driver Board for Desktop Mini Humidifier.
  ESP32S-HiLetgo: HiLetgo ESP-WROOM-32 ESP32 ESP-32S Development Board 2.4GHz Dual-Mode WiFi + Bluetooth Dual Cores Microcontroller The ESP32 integrated with Antenna switches, RF Balun, power amplifiers, low-noise amplifiers, filters, and management modules, and the entire solution occupies the least area of PCB. 2.4 GHz Wi-Fi plus Bluetooth dual-mode chip, with TSMC Ultra-low power consumption 40nm technology,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
  KY-018 Photoresistor Module: KY-018 Photoresistor module, used to measure light intensity. It can determine the presence or absence of light.
  Water Level Sensor: A water level sensor. This sensor operates at 3V to 5V. The Sig (signal) pin outputs an analogue signal that is in proportion to the amount of water in contact with the sensor.
